# Fritzing sketch DHT22 (saved by Fritzing 0.9.3b)

parts:
  Raspberry_Pi_2 = Raspberry Pi 3 [part_number=RPI-3-V1.2]
  DHT22 = Humidity and Temperature Sensor RHT03 [part_number="TEMP/HUM SENSOR"]
  part = Resistor [tolerance=±5% resistance=4.7k package=THT]  # not connected

nets:
  3V3: Raspberry_Pi_2.3v3, DHT22.Vcc
  N1: Raspberry_Pi_2.GIPO16, DHT22.Data-signal
  N2: Raspberry_Pi_2.GND, DHT22.GND_2

notes:
  GPIO 16
  3.3V
